// Logisim project Controlador_P04.circ as structural Verilog: 2 circuits, main circuit main
module main (
  input  D,
  input  T,
  input  Z,
  input  W,
  input  Y,
  input  X,
  input  d2,
  input  d1,
  input  d0,
  output L,
  output q2,
  output q1,
  output q0
);

  LC_ESTADO lc_estado_1 (
    .d2(d2), .d1(d1), .d0(d0), .X(X), .Y(Y), .W(W), .Z(Z), .T(T), .D(D), .q2(q2), .q1(q1), .q0(q0), .L(L));
endmodule

module LC_ESTADO (
  input  d2,
  input  d1,
  input  d0,
  input  X,
  input  Y,
  input  W,
  input  Z,
  input  T,
  input  D,
  output q2,
  output q1,
  output q0,
  output L
);

  wire and_1_out, and_2_out, and_3_out, and_4_out, and_5_out, and_6_out, and_7_out, and_8_out, and_10_out,
       and_11_out, and_12_out, and_13_out, and_14_out, and_15_out, and_16_out, and_17_out, and_18_out,
       or_2_out, or_3_out, xnor_1_out;

  xnor xnor_1 (xnor_1_out, Y, Z);
  and and_1 (and_1_out, ~d2, ~d1, d0);  // AND_Gate
  and and_2 (and_2_out, d2, ~d1, ~d0);  // AND_Gate
  and and_3 (and_3_out, d2, ~d1, d0);  // AND_Gate
  and and_4 (and_4_out, xnor_1_out, and_1_out);
  and and_5 (and_5_out, and_2_out, ~D);  // AND_Gate
  and and_6 (and_6_out, and_3_out, ~T);  // AND_Gate
  xor xor_1 (L, d2, d1);
  or or_1 (q2, and_4_out, and_5_out, and_6_out);
  and and_7 (and_7_out, ~d2, ~d1, d0);  // AND_Gate
  and and_8 (and_8_out, Y, ~Z);  // AND_Gate
  and and_9 (q1, and_7_out, and_8_out);
  or or_2 (or_2_out, ~X, ~W);  // OR_Gate
  and and_10 (and_10_out, Y, Z);
  and and_11 (and_11_out, ~d2, ~d1, ~d0);  // AND_Gate
  and and_12 (and_12_out, ~d2, ~d1, d0);  // AND_Gate
  and and_13 (and_13_out, Y, ~Z, or_2_out);  // AND_Gate
  and and_14 (and_14_out, ~d2, d1);  // AND_Gate
  and and_15 (and_15_out, d2, ~d1, d0);  // AND_Gate
  and and_16 (and_16_out, and_15_out, ~T);  // AND_Gate
  and and_17 (and_17_out, and_11_out, T);
  or or_3 (or_3_out, and_13_out, and_10_out);
  and and_18 (and_18_out, and_12_out, or_3_out);
  or or_4 (q0, and_17_out, and_18_out, and_14_out, and_16_out);
endmodule
